# Fritzing sketch BLE Power Meter Schematic (saved by Fritzing 0.9.4)
breadboards: 1

parts:
  Part1 = Adafruit Feather nRF52 [part_number="Adafruit #3406"]
  S1 = Hall Sensor [part_number=WSH130 package=TO92]
  Part2 = InvenSense MPU6050
  U1 = LIPO-1000mAh [package=lipo-1000]  # not connected

nets:
  VCC: Part1.3.3V, S1.VCC, Part2.VCC
  GND: Part1.GND, S1.GND, Part2.GND
  N1: Part1.SDA, Part2.SDA
  N2: Part1.SCL, Part2.SCL
  N3: Part1.P0.27, S1.OUT

custom parts:
  Hall Sensor: A Hall Sensor
